// Logisim project alu.circ as structural Verilog: 1 circuit, main circuit ALU
module ALU (
  input  [31:0] A,
  input  [31:0] B,
  input  [3:0] ALU_Op,
  output [31:0] Out
);

  wire comparator_1_lt;
  wire [4:0] bit_extender_1_out, bit_extender_2_out;
  wire [31:0] AND, bit_extender_3_out, DIV, DIV2, L, MUL, MUL2, OR, R, REST, SUM, XOR;

  Bit_Extender #(.in_width(32), .out_width(5)) bit_extender_1 (.in(B), .out(bit_extender_1_out));
  Bit_Extender #(.in_width(32), .out_width(5)) bit_extender_2 (.in(B), .out(bit_extender_2_out));
  Shifter #(.width(32)) shifter_1 (.in(A), .\dist (bit_extender_1_out), .out(L));
  Shifter #(.width(32), .shift("lr")) shifter_2 (.in(A), .\dist (bit_extender_2_out), .out(R));
  Adder #(.width(32)) adder_1 (.a(A), .b(B), .out(SUM));  // open: cin, cout
  Multiplier #(.width(32)) multiplier_1 (.a(A), .b(B), .out(MUL));  // open: cin, cout
  Multiplier #(.width(32)) multiplier_2 (.a(A), .b(B), .cout(MUL2));  // open: out, cin
  assign AND = A & B;  // AND_Gate and_1, 32 bits wide
  assign OR = A | B;  // OR_Gate or_1, 32 bits wide
  assign XOR = A ^ B;  // XOR_Gate xor_1, 32 bits wide
  Divider #(.width(32)) divider_1 (.a(A), .b(B), .out(DIV));  // open: upper, rem
  Divider #(.width(32)) divider_2 (.a(A), .b(B), .rem(DIV2));  // open: out, upper
  Subtractor #(.width(32)) subtractor_1 (.a(A), .b(B), .out(REST));  // open: bin, bout
  Comparator #(.width(32)) comparator_1 (.a(A), .b(B), .lt(comparator_1_lt));  // open: gt, eq
  assign bit_extender_3_out = {{31{1'b0}}, comparator_1_lt};  // Bit_Extender bit_extender_3
  Multiplexer #(.select(4), .width(32)) multiplexer_1 (
    .in0(L), .in1(R), .in2(SUM), .in3(AND), .in4(OR), .in5(XOR), .in6(bit_extender_3_out), .in7(MUL),
    .in8(MUL2), .in9(DIV), .in10(DIV2), .in11(REST), .out(Out), .sel(ALU_Op));  // open: in12, in13, in14, in15, en

  // Other names for the same wires on the sheet: Op[3:0] = ALU_Op

  // Notes on the sheet:
  //   Inputs
  //   NOTE
  //   Please do not modify/replace/move/change/delete/etc input and output pins
  //   Outputs
endmodule
