// Logisim project regfile.circ as structural Verilog: 1 circuit, main circuit RegFile
module RegFile (
  input  [4:0] RD,
  input  [31:0] in_2,
  input  [4:0] RS1,
  input  [4:0] RS2,
  input  [31:0] W,
  input  WE,
  input  Clk,
  output [31:0] s0,
  output [31:0] s1,
  output [31:0] t0,
  output [31:0] t1,
  output [31:0] a0,
  output [31:0] ra,
  output [31:0] sp,
  output [31:0] R1,
  output [31:0] R2
);

  wire demultiplexer_1_out8, demultiplexer_1_out9, demultiplexer_1_out10, demultiplexer_1_out11,
       demultiplexer_1_out12, demultiplexer_1_out13, demultiplexer_1_out14, demultiplexer_1_out15,
       demultiplexer_1_out16;
  wire [31:0] register_1_q;

  Register #(.width(32)) register_1 (.D(in_2), .en(demultiplexer_1_out8), .Q(register_1_q), .clk(Clk));  // open: clr
  Multiplexer #(.select(3), .width(32)) multiplexer_1 (.in7(register_1_q));  // open: in0, in1, in2, in3, in4, in5, in6, out, sel, en
  Register #(.width(32)) register_2 (.D(W), .en(demultiplexer_1_out9), .clk(Clk));  // open: Q, clr
  Register #(.width(32)) register_3 (.D(W), .en(demultiplexer_1_out10), .clk(Clk));  // open: Q, clr
  Register #(.width(32)) register_4 (.D(W), .en(demultiplexer_1_out11), .clk(Clk));  // open: Q, clr
  Register #(.width(32)) register_5 (.D(W), .en(demultiplexer_1_out12), .clk(Clk));  // open: Q, clr
  Register #(.width(32)) register_6 (.D(W), .en(demultiplexer_1_out13), .clk(Clk));  // open: Q, clr
  Register #(.width(32)) register_7 (.D(W), .en(demultiplexer_1_out14), .clk(Clk));  // open: Q, clr
  Register #(.width(32)) register_8 (.D(W), .en(demultiplexer_1_out15), .clk(Clk));  // open: Q, clr
  Register #(.width(32)) register_9 (.D(W), .en(demultiplexer_1_out16), .clk(Clk));  // open: Q, clr
  Demultiplexer #(.select(5)) demultiplexer_1 (
    .out8(demultiplexer_1_out8), .out9(demultiplexer_1_out9), .out10(demultiplexer_1_out10),
    .out11(demultiplexer_1_out11), .out12(demultiplexer_1_out12), .out13(demultiplexer_1_out13),
    .out14(demultiplexer_1_out14), .out15(demultiplexer_1_out15), .out16(demultiplexer_1_out16), .in(WE),
    .sel(RD));  // open: out0, out1, out2, out3, out4, out5, out6, out7, out17, out18, out19, out20, out21, out22, out23, out24, out25, out26, out27, out28, out29, out30, out31, en

  // Notes on the sheet:
  //   Write Register
  //   Read Register 1
  //   Read Register 2
  //   Write Data
  //   Write Enable
  //   Clock
  //   NOTE
  //   Please do not modify/replace/move/change/delete/etc input and output pins
  //   These are debug/test outputs from your circuit
  //   Read Data 1
  //   Read Data 2
endmodule
